# Fritzing sketch прототип1 (saved by Fritzing 0.9.3b)
breadboards: 1

parts:
  Часть1 = Arduino Uno (Rev3)
  S1 = Pushbutton [package="[THT]"]
  Часть2 = LED Matrix - Serial Interface - Red/Green/Blue  # not connected
  VCC1 = Battery  # not connected
  J1 = Piezo Speaker
  Q1 = NPN-Transistor [package="TO92 [THT]"]
  7_Segment1 = 7 Segment Display  # not connected
  S3 = Toggle Switch [package=THT]  # not connected

nets:
  N1: Часть1.D2, Q1.B
  N2: Часть1.D3_PWM, S1.Pin_3, S1.Pin_4
  N3: S1.Pin_1, S1.Pin_2, J1.pin1
  N4: J1.pin2, Q1.E
